// Logisim project IT012_Lab01_25521347.circ as structural Verilog: 6 circuits, main circuit Warmup
module TN1 (
  input  A,
  input  B,
  input  A_2,
  input  B_2,
  input  C,
  output F,
  output F_2,
  output F_3,
  output F_4,
  output F_5,
  output F_6,
  output F_7,
  output F_8,
  output F2,
  output F3
);

  wire nand_3_out;

  and and_1 (F_2, A, B);
  nor nor_1 (F_5, A, B);
  xnor xnor_1 (F_7, A, B);
  nand nand_1 (F3, B_2, A_2, C);
  not not_1 (F, A);
  or or_1 (F_3, A, B);
  nand nand_2 (F_4, B, A);
  xor xor_1 (F_6, A, B);
  xor xor_2 (F_8, A_2, B_2, C);
  nand nand_3 (nand_3_out, A_2, B_2);
  nand nand_4 (F2, nand_3_out, C);
endmodule

module TN2 (
  input  X,
  input  Y,
  input  Z,
  output EQ1,
  output EQ2,
  output EQ3,
  output EQ4,
  output EQ5
);

  wire and_1_out, and_2_out, and_3_out, and_4_out, nand_1_out, nor_1_out, not_1_out, not_2_out, not_3_out,
       or_1_out, or_2_out, or_3_out, or_4_out, or_5_out;

  nor nor_1 (nor_1_out, X, Y);
  not not_1 (not_1_out, X);
  not not_2 (not_2_out, Y);
  not not_3 (not_3_out, X);
  and and_1 (and_1_out, not_1_out, not_2_out);
  nand nand_1 (nand_1_out, X, Y);
  or or_1 (or_1_out, X, Y);
  or or_2 (or_2_out, X, Z);
  and and_2 (and_2_out, Z, Y);
  and and_3 (and_3_out, not_3_out, Y);
  or or_3 (or_3_out, X, Y);
  and and_4 (and_4_out, or_1_out, or_2_out);
  or or_4 (or_4_out, X, and_2_out);
  or or_5 (or_5_out, and_3_out, X);
  xnor xnor_1 (EQ1, nor_1_out, and_1_out);
  xnor xnor_2 (EQ2, and_1_out, nand_1_out);
  xnor xnor_3 (EQ3, and_4_out, or_4_out);
  xnor xnor_4 (EQ4, X, or_5_out);
  xnor xnor_5 (EQ5, or_5_out, or_3_out);
endmodule

module Warmup (
  input  A,
  input  B,
  output F
);

  wire not_1_out;

  not not_1 (not_1_out, B);
  and and_1 (F, A, not_1_out);
endmodule

module TN3 (
  input  A,
  input  B,
  input  C,
  input  D,
  output F
);

  wire and_1_out, and_2_out, and_3_out, and_4_out, and_5_out, and_6_out, not_1_out, not_2_out, not_3_out,
       not_4_out;

  not not_1 (not_1_out, A);
  not not_2 (not_2_out, B);
  not not_3 (not_3_out, C);
  not not_4 (not_4_out, D);
  and and_1 (and_1_out, not_1_out, not_2_out, C, not_4_out);
  and and_2 (and_2_out, not_1_out, not_2_out, C, D);
  and and_3 (and_3_out, not_1_out, B, not_3_out, D);
  and and_4 (and_4_out, not_1_out, B, C, D);
  and and_5 (and_5_out, A, not_2_out, C, D);
  and and_6 (and_6_out, A, B, not_3_out, D);
  or or_1 (F, and_1_out, and_2_out, and_3_out, and_4_out, and_5_out, and_6_out);
endmodule

module TN4 (
  input  A,
  input  B,
  input  C,
  input  D,
  output F_can,
  output EQ1,
  output EQ2,
  output F_sop,
  output F_pos
);

  wire and_1_out, and_2_out, and_3_out, and_4_out, and_5_out, and_6_out, and_7_out, and_8_out, and_9_out,
       and_10_out, not_1_out, not_2_out, not_3_out, not_4_out, or_3_out, or_4_out, or_5_out, or_6_out;

  not not_1 (not_1_out, A);
  not not_2 (not_2_out, B);
  not not_3 (not_3_out, C);
  not not_4 (not_4_out, D);
  and and_1 (and_1_out, not_1_out, not_2_out, C);
  and and_2 (and_2_out, not_1_out, B, D);
  and and_3 (and_3_out, not_2_out, C, D);
  and and_4 (and_4_out, B, not_3_out, D);
  and and_5 (and_5_out, not_1_out, not_2_out, C, not_4_out);
  and and_6 (and_6_out, not_1_out, not_2_out, C, D);
  and and_7 (and_7_out, not_1_out, B, D);
  and and_8 (and_8_out, not_1_out, B, C, D);
  and and_9 (and_9_out, A, not_2_out, C, D);
  and and_10 (and_10_out, A, B, not_3_out, D);
  or or_1 (F_can, and_5_out, and_6_out, and_7_out, and_8_out, and_9_out, and_10_out);
  or or_2 (F_sop, and_1_out, and_2_out, and_3_out, and_4_out);
  or or_3 (or_3_out, not_1_out, D);
  or or_4 (or_4_out, not_2_out, D);
  or or_5 (or_5_out, C, B);
  or or_6 (or_6_out, not_1_out, not_2_out, not_3_out);
  xnor xnor_1 (EQ1, F_can, F_sop);
  and and_11 (F_pos, or_3_out, or_4_out, or_5_out, or_6_out);
  xnor xnor_2 (EQ2, F_can, F_pos);
endmodule

module TN5 (
  input  A,
  input  B,
  input  C,
  output F
);

  wire xor_1_out;

  xor xor_1 (xor_1_out, A, B);
  xor xor_2 (F, xor_1_out, C);
endmodule
