// Logisim project IT012_Lab02_25521347.circ as structural Verilog: 6 circuits, main circuit Warmup
module Warmup (
  input  [7:0] A,
  input  [7:0] B,
  output [7:0] S
);

  Adder adder_1 (.a(A), .b(B), .out(S));  // open: cin, cout
  // Probe on S
endmodule

module FA (
  input  A,
  input  B,
  input  Cin,
  output S,
  output Cout
);

  wire and_1_out, and_2_out, xor_1_out;

  xor xor_1 (xor_1_out, A, B);
  and and_1 (and_1_out, A, B);
  and and_2 (and_2_out, Cin, xor_1_out);
  xor xor_2 (S, xor_1_out, Cin);
  or or_1 (Cout, and_1_out, and_2_out);
endmodule

module ADDSUB4 (
  input  [3:0] A,
  input  [3:0] B,
  input  SUB,
  output [3:0] S,
  output C
);

  wire fa_1_cout, fa_2_cout, fa_3_cout, xor_1_out, xor_2_out, xor_3_out, xor_4_out;

  xor xor_1 (xor_1_out, B[0], SUB);
  xor xor_2 (xor_2_out, B[1], SUB);
  xor xor_3 (xor_3_out, B[2], SUB);
  xor xor_4 (xor_4_out, B[3], SUB);
  FA fa_1 (.A(A[0]), .B(xor_1_out), .Cin(SUB), .S(S[0]), .Cout(fa_1_cout));
  FA fa_2 (.A(A[1]), .B(xor_2_out), .Cin(fa_1_cout), .S(S[1]), .Cout(fa_2_cout));
  FA fa_3 (.A(A[2]), .B(xor_3_out), .Cin(fa_2_cout), .S(S[2]), .Cout(fa_3_cout));
  FA fa_4 (.A(A[3]), .B(xor_4_out), .Cin(fa_3_cout), .S(S[3]), .Cout(C));
endmodule

module ALU8 (
  input  [7:0] A,
  input  [7:0] B,
  input  [1:0] OP1,
  input  OP2,
  output [7:0] R,
  output Z
);

  wire [7:0] adder_1_out, adder_2_out, and_1_out, multiplexer_1_out, multiplexer_2_out, not_1_out, or_1_out,
       subtractor_1_out, subtractor_2_out, xor_1_out;

  Adder adder_1 (.a(A), .b(B), .out(adder_1_out));  // open: cin, cout
  Adder adder_2 (.a(A), .b(8'h1), .out(adder_2_out));  // open: cin, cout
  Subtractor subtractor_1 (.a(A), .b(B), .out(subtractor_1_out));  // open: bin, bout
  Subtractor subtractor_2 (.a(A), .b(8'h1), .out(subtractor_2_out));  // open: bin, bout
  assign and_1_out = A & B;  // AND_Gate and_1, 8 bits wide
  assign or_1_out = A | B;  // OR_Gate or_1, 8 bits wide
  assign not_1_out = ~A;  // NOT_Gate not_1, 8 bits wide
  assign xor_1_out = A ^ B;  // XOR_Gate xor_1, 8 bits wide
  Multiplexer #(.select(2), .width(8)) multiplexer_1 (
    .in0(and_1_out), .in1(or_1_out), .in2(not_1_out), .in3(xor_1_out), .out(multiplexer_1_out), .sel(OP1));  // open: en
  Multiplexer #(.select(2), .width(8)) multiplexer_2 (
    .in0(adder_1_out), .in1(adder_2_out), .in2(subtractor_1_out), .in3(subtractor_2_out),
    .out(multiplexer_2_out), .sel(OP1));  // open: en
  Multiplexer #(.width(8)) multiplexer_3 (
    .in0(multiplexer_2_out), .in1(multiplexer_1_out), .out(R), .sel(OP2));  // open: en
  nor nor_1 (Z, R[0], R[1], R[2], R[3], R[4], R[5], R[6], R[7]);
endmodule

module LT (
  input  [7:0] A,
  input  [7:0] B,
  output [7:0] R,
  output R7
);

  Subtractor subtractor_1 (.a(A), .b(B), .out(R));  // open: bin, bout

  assign R7 = R[7];
endmodule

module conLT (
  input  [7:0] A7,
  input  [7:0] B7,
  input  R7
);

  ALU8 alu8_1 (.A(A7), .B(B7));  // open: OP1, OP2, R, Z
endmodule
